// Logisim project 1001s.circ as structural Verilog: 3 circuits, main circuit main
module main (
  input  in_1
);

  wire clock_1_out, counter_1_carry, not_1_out, rom_1_data, shift_register_1_out, \输出_1_out ;
  wire [2:0] register_1_q, \转移_1_n0 ;
  wire [3:0] counter_1_q;

  Counter #(.width(4), .max('hf), .ongoal("stay"), .trigger("rising"), .behavior("new")) counter_1 (
    .Q(counter_1_q), .carry(counter_1_carry), .clk(clock_1_out), .clr(in_1));  // open: load, D, count, preset, down
  ROM #(.addrWidth(4), .dataWidth(1), .Select("low")) rom_1 (.addr(counter_1_q), .data(rom_1_data));
  not not_1 (not_1_out, counter_1_carry);
  \转移  \u_转移_1  (
    .S0(register_1_q[0]), .In(rom_1_data), .S1(register_1_q[1]), .S2(register_1_q[2]), .N0(\转移_1_n0 [0]),
    .N1(\转移_1_n0 [1]), .N2(\转移_1_n0 [2]));
  Register #(.width(3), .trigger("rising"), .Select("low")) register_1 (
    .D(\转移_1_n0 ), .en(not_1_out), .Q(register_1_q), .clk(clock_1_out), .clr(in_1));
  Clock #(.highDuration(1), .lowDuration(1)) clock_1 (.out(clock_1_out));
  \输出  \u_输出_1  (.S0(register_1_q[0]), .S1(register_1_q[1]), .S2(register_1_q[2]), .OUT(\输出_1_out ));
  Shift_Register #(.width(1), .length(16), .parallel("true"), .trigger("rising")) shift_register_1 (
    .shift(not_1_out), .in(\输出_1_out ), .clk(clock_1_out), .out(shift_register_1_out), .clr(in_1));  // open: load, d0, q0, d1, q1, d2, q2, d3, q3, d4, q4, d5, q5, d6, q6, d7, q7, d8, q8, d9, q9, d10, q10, d11, q11, d12, q12, d13, q13, d14, q14, d15, q15

  // Notes on the sheet:
  //   contents of rom_1 (hex, n*v repeats v):
  //   0 0 1 0 1 0 0 1 0 0 1 0 1
endmodule

module \转移  (
  input  S0,
  input  In,
  input  S1,
  input  S2,
  output N0,
  output N1,
  output N2
);

  wire and_2_out, and_3_out, and_4_out, and_5_out, and_6_out, and_7_out, and_8_out, and_9_out, not_1_out,
       not_2_out, not_3_out, not_4_out, not_5_out, not_6_out, not_7_out, not_8_out, not_9_out, not_10_out,
       not_11_out, not_12_out, not_13_out, not_14_out, not_15_out;

  not not_1 (not_1_out, S1);
  not not_2 (not_2_out, S0);
  not not_3 (not_3_out, S0);
  not not_4 (not_4_out, In);
  not not_5 (not_5_out, S1);
  not not_6 (not_6_out, S0);
  not not_7 (not_7_out, S1);
  not not_8 (not_8_out, S0);
  not not_9 (not_9_out, S1);
  not not_10 (not_10_out, In);
  not not_11 (not_11_out, S0);
  not not_12 (not_12_out, In);
  not not_13 (not_13_out, S1);
  not not_14 (not_14_out, S0);
  not not_15 (not_15_out, In);
  and and_1 (N2, S1, S0, In);
  and and_2 (and_2_out, not_1_out, not_2_out, In);
  and and_3 (and_3_out, S1, not_3_out, not_4_out);
  and and_4 (and_4_out, not_5_out, S0, In);
  and and_5 (and_5_out, S1, not_6_out, In);
  and and_6 (and_6_out, S2, not_7_out, not_8_out, In);
  and and_7 (and_7_out, not_9_out, S0, not_10_out);
  and and_8 (and_8_out, S1, not_11_out, not_12_out);
  or or_1 (N1, and_7_out, and_8_out, and_9_out);
  and and_9 (and_9_out, S2, not_13_out, not_14_out, not_15_out);
  or or_2 (N0, and_2_out, and_3_out, and_4_out, and_5_out, and_6_out);
endmodule

module \输出  (
  input  S0,
  input  S1,
  input  S2,
  output OUT
);

  wire not_1_out, not_2_out;

  not not_1 (not_1_out, S1);
  not not_2 (not_2_out, S0);
  and and_1 (OUT, S2, not_1_out, not_2_out);
endmodule
